# Fritzing sketch iWork (saved by Fritzing 0.9.3b)
circuit board: 8.46667cm x 5.64444cm
breadboards: 1

parts:
  Bauteil1 = Photon
  S1 = Momentary Switch [package=ksa_sealed_tac_switch]
  S2 = Momentary Switch [package=ksa_sealed_tac_switch]
  Bauteil2 = OLED Monochrome 128x64 0.96 inch [part_number=326]
  LED1 = LED - 3mm [color="Green (555nm)" package="3 mm [THT]"]
  LED2 = LED - 3mm [color="Red (633nm)" package="3 mm [THT]"]
  LED3 = LED - 3mm [color="White (6500K)" package="3 mm [THT]"]
  S3 = Momentary Switch [package=ksa_sealed_tac_switch]

nets:
  N1: Bauteil1.A0, LED1.anode
  N2: Bauteil1.A1, LED2.anode
  N3: Bauteil1.A2, LED3.anode
  GND: Bauteil1.GND, S1.4, S2.4, Bauteil2.GND, LED1.cathode, LED2.cathode, LED3.cathode, S3.4
  VIN: Bauteil1.VIN, Bauteil2.VIN
  N4: Bauteil1.D0, Bauteil2.MOSI_SDA
  N5: Bauteil1.D1, Bauteil2.SCLK_SCK
  N6: Bauteil1.D2, Bauteil2.DC_SA0
  N7: Bauteil1.D3, Bauteil2.CS
  N8: Bauteil1.D4, Bauteil2.RESET
  N9: Bauteil1.D5, S1.3
  N10: Bauteil1.D6, S2.3
  N11: Bauteil1.D7, S3.3

custom parts:
  OLED Monochrome 128x64 0.96 inch: These displays are small, only about 1" diameter, but very readable due to the high contrast of an OLED display. This display is made of 128x64 individual white OLED pixels, each one is turned on or off by the controller chip. Because the display makes its own light, no backlight is required. This reduces the power required to run the OLED and is why the display has such high contrast; we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
